# Fritzing sketch garageDoor (saved by Fritzing 0.9.3b)
breadboards: 1

parts:
  U1 = NodeMCU V1.0  # not connected
  Q1 = PNP-Transistor [package="TO92 [THT]"]
  J1 = Screw terminal - 2 pins [package=THT]
  HC-SR04_Sensor_1 = HC-SR04 Ultrasonic Distance Sensor  # not connected

nets:
  N1: Q1.E, J1.pin2
  N2: Q1.C, J1.pin1

notes:
  Screw terminals go to garage door opener

custom parts:
  NodeMCU V1.0: ESP8266 based NodeMCU
